# Fritzing sketch fritzing (saved by Fritzing 0.9.3b)
circuit board: 6.08334cm x 4.65641cm
breadboards: 1

parts:
  ESP-01 = ESP8266 WiFi Module [part_number=ESP8266]
  HX-711 = HX711 Weighing Sensor Module
  IRL_Z34N = Basic FET N-Channel [package="TO220 [THT]"]
  1700 = Voltage Regulator [package=to-92]
  U3 = attiny85 [package=dip]
  R050 = Resettable Fuse PTC [package=ptc]
  R1 = Resistor [tolerance=±5% resistance=10k package=THT]
  R2 = Resistor [tolerance=±5% resistance=10k package=THT]
  R3 = Resistor [tolerance=±5% resistance=10k package=THT]
  J1 = female pin header, 6 pins [form="♀ (female)"]
  J2 = female pin header, 2 pins [form="♀ (female)"]
  U4 = Molex Picoblade Series Header [part_number=0532610219 package=Picoblade-53261-0219]
  R4 = Resistor [tolerance=±5% resistance=10k package=THT]

nets:
  3.3V: ESP-01.VCC, ESP-01.CH_PD, HX-711.VCC, U3.Pin_8, R050.1, R1.Pin_1, R2.Pin_1, R4.Pin_0
  N1: ESP-01.GPIO_0, U3.Pin_5, R1.Pin_0, J2.pin2
  N2: ESP-01.GPIO_2, U3.Pin_7, R2.Pin_0, J2.pin1
  N3: ESP-01.GND, IRL_Z34N.drain
  GND: HX-711.GND, IRL_Z34N.source, 1700.GND, U3.Pin_4, R3.Pin_0, U4.2
  N4: HX-711.DO/RX, U3.Pin_2
  N5: HX-711.CK/TX, U3.Pin_3
  N6: HX-711.E+, J1.pin1
  N7: HX-711.E-, J1.pin2
  N8: HX-711.A+, J1.pin3
  N9: HX-711.A-, J1.pin4
  N10: HX-711.B+, J1.pin5
  N11: HX-711.B-, J1.pin6
  N12: IRL_Z34N.gate, U3.Pin_6, R3.Pin_1
  N13: 1700.IN, U4.1
  N14: 1700.OUT, R050.2
  N15: U3.Pin_1, R4.Pin_1

notes:
  SDA
  SCL

custom parts:
  ESP8266 WiFi Module: Generic WiFi Module based on the ESP8266 with onboard PCB antenna and UART communications
